// Digital circuit overture.dig as structural Verilog
module overture (
  input  C_0,
  input  C_1,
  input  C_2,
  input  [7:0] A_0,
  input  [7:0] B_0,
  input  clk,
  output [7:0] O_0
);

  wire and_5_out, and_6_out, and_7_out, and_8_out, and_9_out, and_10_out, and_11_out, and_25_out, and_26_out,
       and_27_out, and_28_out, and_29_out, and_30_out, and_31_out, and_32_out, and_39_out, and_40_out,
       and_41_out, and_42_out, and_43_out, and_44_out, and_45_out, and_46_out, and_48_out, and_49_out,
       and_50_out, and_51_out, and_53_out, and_54_out, and_55_out, and_56_out, and_99_out, and_100_out,
       and_101_out, and_102_out, and_103_out, and_104_out, and_105_out, and_106_out, and_111_out,
       and_112_out, and_113_out, and_114_out, and_115_out, and_116_out, and_117_out, and_121_out,
       and_122_out, and_123_out, and_124_out, and_125_out, and_126_out, and_127_out, and_128_out,
       and_129_out, and_130_out, and_131_out, and_132_out, and_133_out, and_134_out, and_135_out,
       and_136_out, and_137_out, and_138_out, and_139_out, and_140_out, and_141_out, and_142_out,
       and_143_out, and_144_out, and_145_out, and_146_out, and_147_out, and_148_out, and_149_out,
       and_150_out, and_151_out, and_152_out, and_153_out, and_154_out, and_155_out, and_156_out,
       and_157_out, and_158_out, and_159_out, and_160_out, and_161_out, and_162_out, and_163_out,
       and_164_out, and_165_out, and_166_out, and_167_out, and_168_out, and_169_out, and_170_out,
       and_171_out, and_172_out, and_173_out, and_174_out, and_175_out, and_177_out, and_178_out,
       and_179_out, and_180_out, and_181_out, and_182_out, and_183_out, and_184_out, and_185_out,
       and_186_out, and_187_out, and_188_out, and_189_out, and_190_out, and_191_out, and_192_out,
       and_193_out, and_194_out, and_195_out, and_196_out, and_197_out, and_198_out, and_199_out,
       and_200_out, and_201_out, and_202_out, and_203_out, and_204_out, and_205_out, and_206_out,
       and_207_out, and_208_out, and_209_out, and_210_out, and_211_out, dipswitch_1_out, dipswitch_2_out,
       dipswitch_3_out, dipswitch_4_out, dipswitch_5_out, nand_1_out, nand_2_out, nand_3_out, nand_4_out,
       nand_5_out, nand_6_out, nand_7_out, nand_8_out, nand_9_out, nand_10_out, nand_11_out, nand_12_out,
       nand_13_out, nand_14_out, nand_15_out, nand_16_out, nand_18_out, nand_20_out, nand_22_out,
       nand_24_out, nand_25_out, nand_26_out, nand_27_out, nand_28_out, nand_29_out, nand_30_out,
       nand_31_out, nand_32_out, nand_33_out, nand_34_out, nand_35_out, nand_36_out, nand_37_out,
       nand_38_out, nand_39_out, nand_40_out, nand_42_out, nand_44_out, nand_46_out, nand_48_out,
       nand_57_out, nand_58_out, nand_59_out, nand_60_out, nand_61_out, nand_62_out, nand_63_out,
       nand_64_out, nand_65_out, nand_66_out, nand_67_out, nand_68_out, nand_69_out, nand_70_out,
       nand_71_out, nand_72_out, nand_73_out, nand_74_out, nand_75_out, nand_76_out, nand_77_out,
       nand_78_out, nand_79_out, nand_80_out, nand_81_out, nand_82_out, nand_83_out, nand_84_out,
       nand_85_out, nand_86_out, nand_87_out, nand_88_out, nand_89_out, nand_90_out, nand_91_out,
       nand_92_out, nand_93_out, nand_94_out, nand_95_out, nand_96_out, nand_97_out, nand_98_out,
       nand_99_out, nand_100_out, nand_101_out, nand_102_out, nand_103_out, nand_104_out, nand_105_out,
       nand_106_out, nand_107_out, nand_108_out, nand_109_out, nand_110_out, nand_111_out, nand_112_out,
       nor_9_out, nor_10_out, nor_11_out, nor_12_out, nor_13_out, nor_14_out, nor_15_out, nor_16_out,
       nor_17_out, nor_18_out, nor_19_out, nor_20_out, nor_21_out, nor_22_out, nor_23_out, nor_24_out,
       nor_25_out, nor_26_out, nor_27_out, nor_28_out, nor_29_out, nor_30_out, nor_31_out, nor_32_out,
       nor_33_out, nor_34_out, not_1_out, not_2_out, not_3_out, not_4_out, not_5_out, not_6_out, not_7_out,
       not_8_out, not_9_out, not_10_out, not_11_out, not_12_out, not_13_out, not_14_out, not_15_out,
       not_16_out, not_17_out, not_18_out, not_19_out, not_20_out, not_21_out, not_22_out, not_23_out,
       not_24_out, not_25_out, notconnected_2_out, notconnected_3_out, notconnected_4_out,
       notconnected_5_out, notconnected_9_out, notconnected_14_out, notconnected_18_out, notconnected_19_out,
       notconnected_20_out, notconnected_21_out, or_16_out, or_17_out, or_18_out, or_19_out, or_20_out,
       or_21_out, or_22_out, or_23_out, or_25_out, or_66_out, or_67_out, or_68_out, or_69_out, or_70_out,
       or_71_out, or_72_out, or_73_out, or_74_out, or_75_out, or_76_out, or_77_out, or_78_out, or_79_out,
       or_80_out, or_81_out, xor_9_out, xor_10_out, xor_11_out, xor_12_out, xor_13_out, xor_14_out,
       xor_15_out, xor_16_out, xor_23_out, xor_24_out, xor_25_out, xor_26_out, xor_27_out, xor_28_out,
       xor_29_out, xor_30_out, xor_41_out, xor_42_out, xor_43_out, xor_44_out, xor_45_out, xor_46_out,
       xor_47_out, xor_48_out, xor_49_out, xor_50_out, xor_51_out, xor_52_out, xor_53_out, xor_54_out,
       xor_55_out, xor_56_out, xor_57_out, xor_58_out, xor_59_out, xor_60_out, xor_61_out, xor_62_out,
       xor_63_out, xor_64_out, xor_65_out, xor_66_out, xor_67_out, xor_68_out, xor_69_out, xor_70_out,
       xor_71_out, xor_72_out;
  wire [7:0] and_16_out, and_24_out, and_52_out, and_92_out, and_93_out, and_94_out, and_95_out, and_96_out,
       and_120_out, nand_47_out, nand_56_out, nor_8_out, notconnected_1_out, notconnected_6_out,
       notconnected_7_out, notconnected_8_out, notconnected_10_out, notconnected_11_out, notconnected_12_out,
       notconnected_13_out, notconnected_15_out, notconnected_16_out, notconnected_17_out, or_8_out,
       or_24_out, or_62_out, or_63_out, or_64_out, or_65_out, xor_8_out, xor_36_out, xor_40_out;

  DipSwitch dipswitch_1 (.out(dipswitch_1_out));
  and and_1 (and_16_out[0], dipswitch_1_out, 1'b0);
  and and_2 (and_16_out[1], dipswitch_1_out, 1'b0);
  and and_3 (and_16_out[2], dipswitch_1_out, 1'b0);
  // And and_4 has open pins: In_1=and_5_out, In_2=nand_47_out[7], out=open
  xor xor_1 (xor_8_out[7], nand_47_out[7], and_5_out);
  and and_5 (and_5_out, and_6_out, nand_47_out[6]);
  xor xor_2 (xor_8_out[6], nand_47_out[6], and_6_out);
  and and_6 (and_6_out, and_7_out, nand_47_out[5]);
  xor xor_3 (xor_8_out[5], nand_47_out[5], and_7_out);
  and and_7 (and_7_out, and_8_out, nand_47_out[4]);
  xor xor_4 (xor_8_out[4], nand_47_out[4], and_8_out);
  and and_8 (and_8_out, and_9_out, nand_47_out[3]);
  xor xor_5 (xor_8_out[3], nand_47_out[3], and_9_out);
  and and_9 (and_9_out, and_10_out, nand_47_out[2]);
  xor xor_6 (xor_8_out[2], nand_47_out[2], and_10_out);
  and and_10 (and_10_out, and_11_out, nand_47_out[1]);
  xor xor_7 (xor_8_out[1], nand_47_out[1], and_11_out);
  and and_11 (and_11_out, 1'b1, nand_47_out[0]);
  xor xor_8 (xor_8_out[0], nand_47_out[0], 1'b1);
  and and_12 (and_16_out[3], dipswitch_1_out, 1'b0);
  and and_13 (and_16_out[4], dipswitch_1_out, 1'b0);
  and and_14 (and_16_out[5], dipswitch_1_out, 1'b0);
  and and_15 (and_16_out[6], dipswitch_1_out, 1'b0);
  not not_1 (not_1_out, dipswitch_1_out);
  and and_16 (and_16_out[7], dipswitch_1_out, 1'b0);
  or or_1 (or_8_out[0], and_24_out[0], and_16_out[0]);
  or or_2 (or_8_out[1], and_24_out[1], and_16_out[1]);
  or or_3 (or_8_out[2], and_24_out[2], and_16_out[2]);
  and and_17 (and_24_out[0], not_1_out, xor_8_out[0]);
  and and_18 (and_24_out[1], not_1_out, xor_8_out[1]);
  and and_19 (and_24_out[2], not_1_out, xor_8_out[2]);
  and and_20 (and_24_out[3], not_1_out, xor_8_out[3]);
  and and_21 (and_24_out[4], not_1_out, xor_8_out[4]);
  and and_22 (and_24_out[5], not_1_out, xor_8_out[5]);
  and and_23 (and_24_out[6], not_1_out, xor_8_out[6]);
  and and_24 (and_24_out[7], not_1_out, xor_8_out[7]);
  or or_4 (or_8_out[3], and_24_out[3], and_16_out[3]);
  or or_5 (or_8_out[4], and_24_out[4], and_16_out[4]);
  or or_6 (or_8_out[5], and_24_out[5], and_16_out[5]);
  or or_7 (or_8_out[6], and_24_out[6], and_16_out[6]);
  or or_8 (or_8_out[7], and_24_out[7], and_16_out[7]);
  nand nand_1 (nand_1_out, nand_4_out, nand_2_out);
  nand nand_2 (nand_2_out, nand_1_out, clk);
  nand nand_3 (nand_3_out, nand_2_out, clk, nand_4_out);
  nand nand_4 (nand_4_out, nand_3_out, or_8_out[6]);
  nand nand_5 (nand_5_out, nand_8_out, nand_6_out);
  nand nand_6 (nand_6_out, nand_5_out, clk);
  nand nand_7 (nand_7_out, nand_6_out, clk, nand_8_out);
  nand nand_8 (nand_8_out, nand_7_out, or_8_out[4]);
  nand nand_9 (nand_9_out, nand_12_out, nand_10_out);
  nand nand_10 (nand_10_out, nand_9_out, clk);
  nand nand_11 (nand_11_out, nand_10_out, clk, nand_12_out);
  nand nand_12 (nand_12_out, nand_11_out, or_8_out[2]);
  nand nand_13 (nand_13_out, nand_16_out, nand_14_out);
  nand nand_14 (nand_14_out, nand_13_out, clk);
  nand nand_15 (nand_15_out, nand_14_out, clk, nand_16_out);
  nand nand_16 (nand_16_out, nand_15_out, or_8_out[0]);
  nand nand_17 (nand_47_out[6], nand_2_out, nand_18_out);
  nand nand_18 (nand_18_out, nand_47_out[6], nand_3_out);
  nand nand_19 (nand_47_out[4], nand_6_out, nand_20_out);
  nand nand_20 (nand_20_out, nand_47_out[4], nand_7_out);
  nand nand_21 (nand_47_out[2], nand_10_out, nand_22_out);
  nand nand_22 (nand_22_out, nand_47_out[2], nand_11_out);
  nand nand_23 (nand_47_out[0], nand_14_out, nand_24_out);
  nand nand_24 (nand_24_out, nand_47_out[0], nand_15_out);
  and and_25 (and_25_out, nand_47_out[6], 1'b0);
  and and_26 (and_26_out, nand_47_out[4], 1'b0);
  and and_27 (and_27_out, nand_47_out[2], 1'b0);
  and and_28 (and_28_out, nand_47_out[0], 1'b0);
  nand nand_25 (nand_25_out, nand_28_out, nand_26_out);
  nand nand_26 (nand_26_out, nand_25_out, clk);
  nand nand_27 (nand_27_out, nand_26_out, clk, nand_28_out);
  nand nand_28 (nand_28_out, nand_27_out, or_8_out[7]);
  nand nand_29 (nand_29_out, nand_32_out, nand_30_out);
  nand nand_30 (nand_30_out, nand_29_out, clk);
  nand nand_31 (nand_31_out, nand_30_out, clk, nand_32_out);
  nand nand_32 (nand_32_out, nand_31_out, or_8_out[5]);
  nand nand_33 (nand_33_out, nand_36_out, nand_34_out);
  nand nand_34 (nand_34_out, nand_33_out, clk);
  nand nand_35 (nand_35_out, nand_34_out, clk, nand_36_out);
  nand nand_36 (nand_36_out, nand_35_out, or_8_out[3]);
  nand nand_37 (nand_37_out, nand_40_out, nand_38_out);
  nand nand_38 (nand_38_out, nand_37_out, clk);
  nand nand_39 (nand_39_out, nand_38_out, clk, nand_40_out);
  nand nand_40 (nand_40_out, nand_39_out, or_8_out[1]);
  nand nand_41 (nand_47_out[7], nand_26_out, nand_42_out);
  nand nand_42 (nand_42_out, nand_47_out[7], nand_27_out);
  and and_29 (and_29_out, nand_47_out[7], 1'b0);
  nand nand_43 (nand_47_out[5], nand_30_out, nand_44_out);
  nand nand_44 (nand_44_out, nand_47_out[5], nand_31_out);
  and and_30 (and_30_out, nand_47_out[5], 1'b0);
  nand nand_45 (nand_47_out[3], nand_34_out, nand_46_out);
  nand nand_46 (nand_46_out, nand_47_out[3], nand_35_out);
  and and_31 (and_31_out, nand_47_out[3], 1'b0);
  nand nand_47 (nand_47_out[1], nand_38_out, nand_48_out);
  nand nand_48 (nand_48_out, nand_47_out[1], nand_39_out);
  and and_32 (and_32_out, nand_47_out[1], 1'b0);
  ROM #(.AddrBits(8), .isProgramMemory("true"), .Bits(8)) rom_1 (.sel(dipswitch_2_out));  // open: A, D
  DipSwitch dipswitch_2 (.out(dipswitch_2_out));
  xor xor_9 (xor_9_out, B_0[7], and_112_out);
  xor xor_10 (xor_10_out, B_0[6], and_112_out);
  xor xor_11 (xor_11_out, B_0[5], and_112_out);
  xor xor_12 (xor_12_out, B_0[4], and_112_out);
  xor xor_13 (xor_13_out, B_0[3], and_112_out);
  xor xor_14 (xor_14_out, B_0[2], and_112_out);
  xor xor_15 (xor_15_out, B_0[1], and_112_out);
  xor xor_16 (xor_16_out, B_0[0], and_112_out);
  and and_33 (and_52_out[0], B_0[0], A_0[0]);
  nand nand_49 (nand_56_out[0], B_0[0], A_0[0]);
  or or_9 (or_24_out[0], B_0[0], A_0[0]);
  nor nor_1 (nor_8_out[0], B_0[0], A_0[0]);
  xor xor_17 (xor_36_out[0], B_0[0], A_0[0]);
  and and_34 (and_52_out[1], B_0[1], A_0[1]);
  nand nand_50 (nand_56_out[1], B_0[1], A_0[1]);
  or or_10 (or_24_out[1], B_0[1], A_0[1]);
  nor nor_2 (nor_8_out[1], B_0[1], A_0[1]);
  xor xor_18 (xor_36_out[1], B_0[1], A_0[1]);
  and and_35 (and_52_out[2], B_0[2], A_0[2]);
  nand nand_51 (nand_56_out[2], B_0[2], A_0[2]);
  or or_11 (or_24_out[2], B_0[2], A_0[2]);
  nor nor_3 (nor_8_out[2], B_0[2], A_0[2]);
  xor xor_19 (xor_36_out[2], B_0[2], A_0[2]);
  and and_36 (and_52_out[3], B_0[3], A_0[3]);
  and and_37 (and_52_out[4], B_0[4], A_0[4]);
  nand nand_52 (nand_56_out[3], B_0[3], A_0[3]);
  nand nand_53 (nand_56_out[4], B_0[4], A_0[4]);
  or or_12 (or_24_out[3], B_0[3], A_0[3]);
  or or_13 (or_24_out[4], B_0[4], A_0[4]);
  nor nor_4 (nor_8_out[3], B_0[3], A_0[3]);
  nor nor_5 (nor_8_out[4], B_0[4], A_0[4]);
  xor xor_20 (xor_36_out[3], B_0[3], A_0[3]);
  xor xor_21 (xor_36_out[4], B_0[4], A_0[4]);
  and and_38 (and_52_out[5], B_0[5], A_0[5]);
  nand nand_54 (nand_56_out[5], B_0[5], A_0[5]);
  or or_14 (or_24_out[5], B_0[5], A_0[5]);
  nor nor_6 (nor_8_out[5], B_0[5], A_0[5]);
  xor xor_22 (xor_36_out[5], B_0[5], A_0[5]);
  and and_39 (and_39_out, xor_9_out, A_0[7]);
  xor xor_23 (xor_23_out, A_0[7], xor_9_out);
  and and_40 (and_40_out, xor_10_out, A_0[6]);
  xor xor_24 (xor_24_out, A_0[6], xor_10_out);
  and and_41 (and_41_out, xor_11_out, A_0[5]);
  xor xor_25 (xor_25_out, A_0[5], xor_11_out);
  and and_42 (and_42_out, xor_12_out, A_0[4]);
  xor xor_26 (xor_26_out, A_0[4], xor_12_out);
  and and_43 (and_43_out, xor_13_out, A_0[3]);
  xor xor_27 (xor_27_out, A_0[3], xor_13_out);
  and and_44 (and_44_out, xor_14_out, A_0[2]);
  xor xor_28 (xor_28_out, A_0[2], xor_14_out);
  and and_45 (and_45_out, xor_15_out, A_0[1]);
  xor xor_29 (xor_29_out, A_0[1], xor_15_out);
  and and_46 (and_46_out, xor_16_out, A_0[0]);
  xor xor_30 (xor_30_out, A_0[0], xor_16_out);
  and and_47 (and_52_out[6], B_0[6], A_0[6]);
  nand nand_55 (nand_56_out[6], B_0[6], A_0[6]);
  or or_15 (or_24_out[6], B_0[6], A_0[6]);
  nor nor_7 (nor_8_out[6], B_0[6], A_0[6]);
  xor xor_31 (xor_36_out[6], B_0[6], A_0[6]);
  or or_16 (or_16_out, and_39_out, and_48_out);
  and and_48 (and_48_out, xor_23_out, or_17_out);
  xor xor_32 (xor_40_out[7], xor_23_out, or_17_out);
  or or_17 (or_17_out, and_40_out, and_49_out);
  and and_49 (and_49_out, xor_24_out, or_18_out);
  xor xor_33 (xor_40_out[6], xor_24_out, or_18_out);
  or or_18 (or_18_out, and_41_out, and_50_out);
  and and_50 (and_50_out, xor_25_out, or_19_out);
  xor xor_34 (xor_40_out[5], xor_25_out, or_19_out);
  or or_19 (or_19_out, and_42_out, and_51_out);
  and and_51 (and_51_out, xor_26_out, or_20_out);
  xor xor_35 (xor_40_out[4], xor_26_out, or_20_out);
  or or_20 (or_20_out, and_43_out, and_53_out);
  or or_21 (or_21_out, and_44_out, and_54_out);
  or or_22 (or_22_out, and_45_out, and_55_out);
  or or_23 (or_23_out, and_46_out, and_56_out);
  and and_52 (and_52_out[7], B_0[7], A_0[7]);
  nand nand_56 (nand_56_out[7], B_0[7], A_0[7]);
  or or_24 (or_24_out[7], B_0[7], A_0[7]);
  nor nor_8 (nor_8_out[7], B_0[7], A_0[7]);
  xor xor_36 (xor_36_out[7], B_0[7], A_0[7]);
  and and_53 (and_53_out, xor_27_out, or_21_out);
  xor xor_37 (xor_40_out[3], xor_27_out, or_21_out);
  and and_54 (and_54_out, xor_28_out, or_22_out);
  xor xor_38 (xor_40_out[2], xor_28_out, or_22_out);
  and and_55 (and_55_out, xor_29_out, or_23_out);
  xor xor_39 (xor_40_out[1], xor_29_out, or_23_out);
  and and_56 (and_56_out, xor_30_out, and_112_out);
  xor xor_40 (xor_40_out[0], xor_30_out, and_112_out);
  and and_57 (and_92_out[0], and_113_out, and_52_out[0]);
  and and_58 (and_92_out[1], and_113_out, and_52_out[1]);
  and and_59 (and_93_out[0], and_114_out, nand_56_out[0]);
  and and_60 (and_93_out[1], and_114_out, nand_56_out[1]);
  and and_61 (and_94_out[0], and_115_out, or_24_out[0]);
  and and_62 (and_94_out[1], and_115_out, or_24_out[1]);
  and and_63 (and_95_out[0], and_116_out, nor_8_out[0]);
  and and_64 (and_95_out[1], and_116_out, nor_8_out[1]);
  and and_65 (and_96_out[0], and_117_out, xor_36_out[0]);
  and and_66 (and_96_out[1], and_117_out, xor_36_out[1]);
  and and_67 (and_92_out[2], and_113_out, and_52_out[2]);
  and and_68 (and_93_out[2], and_114_out, nand_56_out[2]);
  and and_69 (and_94_out[2], and_115_out, or_24_out[2]);
  and and_70 (and_95_out[2], and_116_out, nor_8_out[2]);
  and and_71 (and_96_out[2], and_117_out, xor_36_out[2]);
  and and_72 (and_92_out[3], and_113_out, and_52_out[3]);
  and and_73 (and_93_out[3], and_114_out, nand_56_out[3]);
  and and_74 (and_94_out[3], and_115_out, or_24_out[3]);
  and and_75 (and_95_out[3], and_116_out, nor_8_out[3]);
  and and_76 (and_96_out[3], and_117_out, xor_36_out[3]);
  and and_77 (and_92_out[4], and_113_out, and_52_out[4]);
  and and_78 (and_92_out[5], and_113_out, and_52_out[5]);
  and and_79 (and_93_out[4], and_114_out, nand_56_out[4]);
  and and_80 (and_93_out[5], and_114_out, nand_56_out[5]);
  and and_81 (and_94_out[4], and_115_out, or_24_out[4]);
  and and_82 (and_94_out[5], and_115_out, or_24_out[5]);
  and and_83 (and_95_out[4], and_116_out, nor_8_out[4]);
  and and_84 (and_95_out[5], and_116_out, nor_8_out[5]);
  and and_85 (and_96_out[4], and_117_out, xor_36_out[4]);
  and and_86 (and_96_out[5], and_117_out, xor_36_out[5]);
  and and_87 (and_92_out[6], and_113_out, and_52_out[6]);
  and and_88 (and_93_out[6], and_114_out, nand_56_out[6]);
  and and_89 (and_94_out[6], and_115_out, or_24_out[6]);
  and and_90 (and_95_out[6], and_116_out, nor_8_out[6]);
  and and_91 (and_96_out[6], and_117_out, xor_36_out[6]);
  and and_92 (and_92_out[7], and_113_out, and_52_out[7]);
  and and_93 (and_93_out[7], and_114_out, nand_56_out[7]);
  and and_94 (and_94_out[7], and_115_out, or_24_out[7]);
  and and_95 (and_95_out[7], and_116_out, nor_8_out[7]);
  and and_96 (and_96_out[7], and_117_out, xor_36_out[7]);
  not not_2 (not_2_out, C_2);
  and and_97 (and_120_out[0], or_25_out, xor_40_out[0]);
  not not_3 (not_3_out, C_1);
  not not_4 (not_4_out, C_1);
  and and_98 (and_120_out[1], or_25_out, xor_40_out[1]);
  not not_5 (not_5_out, C_0);
  and and_99 (and_99_out, not_5_out, not_3_out);
  and and_100 (and_100_out, C_0, not_3_out);
  and and_101 (and_101_out, not_5_out, C_1);
  and and_102 (and_102_out, C_1, C_0);
  not not_6 (not_6_out, C_2);
  not not_7 (not_7_out, C_0);
  and and_103 (and_103_out, not_7_out, not_4_out);
  and and_104 (and_104_out, C_0, not_4_out);
  and and_105 (and_105_out, not_7_out, C_1);
  and and_106 (and_106_out, C_1, C_0);
  not not_8 (not_8_out, not_2_out);
  and and_107 (and_120_out[2], or_25_out, xor_40_out[2]);
  and and_108 (and_120_out[3], or_25_out, xor_40_out[3]);
  and and_109 (and_120_out[4], or_25_out, xor_40_out[4]);
  // And and_110 has open pins: In_1=and_99_out, In_2=not_6_out, out=open
  and and_111 (and_111_out, and_100_out, not_6_out);
  and and_112 (and_112_out, and_101_out, not_6_out);
  and and_113 (and_113_out, and_102_out, not_6_out);
  and and_114 (and_114_out, and_103_out, not_8_out);
  and and_115 (and_115_out, and_104_out, not_8_out);
  and and_116 (and_116_out, and_105_out, not_8_out);
  and and_117 (and_117_out, and_106_out, not_8_out);
  and and_118 (and_120_out[5], or_25_out, xor_40_out[5]);
  and and_119 (and_120_out[6], or_25_out, xor_40_out[6]);
  and and_120 (and_120_out[7], or_25_out, xor_40_out[7]);
  or or_25 (or_25_out, and_111_out, and_112_out);
  or or_26 (O_0[0], and_120_out[0], or_62_out[0]);
  or or_27 (or_62_out[0], and_92_out[0], or_63_out[0]);
  or or_28 (or_63_out[0], and_93_out[0], or_64_out[0]);
  or or_29 (or_64_out[0], and_94_out[0], or_65_out[0]);
  or or_30 (or_65_out[0], and_95_out[0], and_96_out[0]);
  or or_31 (O_0[1], and_120_out[1], or_62_out[1]);
  or or_32 (or_62_out[1], and_92_out[1], or_63_out[1]);
  or or_33 (or_63_out[1], and_93_out[1], or_64_out[1]);
  or or_34 (or_64_out[1], and_94_out[1], or_65_out[1]);
  or or_35 (or_65_out[1], and_95_out[1], and_96_out[1]);
  or or_36 (O_0[2], and_120_out[2], or_62_out[2]);
  or or_37 (or_62_out[2], and_92_out[2], or_63_out[2]);
  or or_38 (or_63_out[2], and_93_out[2], or_64_out[2]);
  or or_39 (or_64_out[2], and_94_out[2], or_65_out[2]);
  or or_40 (or_65_out[2], and_95_out[2], and_96_out[2]);
  or or_41 (O_0[3], and_120_out[3], or_62_out[3]);
  or or_42 (O_0[4], and_120_out[4], or_62_out[4]);
  or or_43 (or_62_out[3], and_92_out[3], or_63_out[3]);
  or or_44 (or_62_out[4], and_92_out[4], or_63_out[4]);
  or or_45 (or_63_out[3], and_93_out[3], or_64_out[3]);
  or or_46 (or_63_out[4], and_93_out[4], or_64_out[4]);
  or or_47 (or_64_out[3], and_94_out[3], or_65_out[3]);
  or or_48 (or_64_out[4], and_94_out[4], or_65_out[4]);
  or or_49 (or_65_out[3], and_95_out[3], and_96_out[3]);
  or or_50 (or_65_out[4], and_95_out[4], and_96_out[4]);
  or or_51 (O_0[5], and_120_out[5], or_62_out[5]);
  or or_52 (or_62_out[5], and_92_out[5], or_63_out[5]);
  or or_53 (or_63_out[5], and_93_out[5], or_64_out[5]);
  or or_54 (or_64_out[5], and_94_out[5], or_65_out[5]);
  or or_55 (or_65_out[5], and_95_out[5], and_96_out[5]);
  or or_56 (O_0[6], and_120_out[6], or_62_out[6]);
  or or_57 (or_62_out[6], and_92_out[6], or_63_out[6]);
  or or_58 (or_63_out[6], and_93_out[6], or_64_out[6]);
  or or_59 (or_64_out[6], and_94_out[6], or_65_out[6]);
  or or_60 (or_65_out[6], and_95_out[6], and_96_out[6]);
  or or_61 (O_0[7], and_120_out[7], or_62_out[7]);
  or or_62 (or_62_out[7], and_92_out[7], or_63_out[7]);
  or or_63 (or_63_out[7], and_93_out[7], or_64_out[7]);
  or or_64 (or_64_out[7], and_94_out[7], or_65_out[7]);
  or or_65 (or_65_out[7], and_95_out[7], and_96_out[7]);
  // NotConnected on notconnected_1_out[0]
  // NotConnected on notconnected_2_out
  // NotConnected on notconnected_3_out
  // NotConnected on notconnected_4_out
  // NotConnected on notconnected_5_out
  // NotConnected on notconnected_6_out
  // NotConnected on notconnected_7_out
  // NotConnected on notconnected_8_out
  nand nand_57 (nand_57_out, nand_60_out, nand_58_out);
  nand nand_58 (nand_58_out, nand_57_out, notconnected_2_out);
  nand nand_59 (nand_59_out, nand_58_out, notconnected_2_out, nand_60_out);
  nand nand_60 (nand_60_out, nand_59_out, notconnected_1_out[6]);
  nand nand_61 (nand_61_out, nand_64_out, nand_62_out);
  nand nand_62 (nand_62_out, nand_61_out, notconnected_2_out);
  nand nand_63 (nand_63_out, nand_62_out, notconnected_2_out, nand_64_out);
  nand nand_64 (nand_64_out, nand_63_out, notconnected_1_out[4]);
  nand nand_65 (nand_65_out, nand_68_out, nand_66_out);
  nand nand_66 (nand_66_out, nand_65_out, notconnected_2_out);
  nand nand_67 (nand_67_out, nand_66_out, notconnected_2_out, nand_68_out);
  nand nand_68 (nand_68_out, nand_67_out, notconnected_1_out[2]);
  nand nand_69 (nand_69_out, nand_72_out, nand_70_out);
  nand nand_70 (nand_70_out, nand_69_out, notconnected_2_out);
  nand nand_71 (nand_71_out, nand_70_out, notconnected_2_out, nand_72_out);
  nand nand_72 (nand_72_out, nand_71_out, notconnected_1_out[0]);
  DipSwitch dipswitch_3 (.out(dipswitch_3_out));
  DipSwitch dipswitch_4 (.out(dipswitch_4_out));
  DipSwitch dipswitch_5 (.out(dipswitch_5_out));
  not not_9 (not_9_out, notconnected_6_out[7]);
  and and_121 (and_121_out, notconnected_4_out, notconnected_6_out[7]);
  not not_10 (not_10_out, notconnected_6_out[6]);
  and and_122 (and_122_out, notconnected_4_out, notconnected_6_out[6]);
  not not_11 (not_11_out, notconnected_6_out[5]);
  and and_123 (and_123_out, notconnected_4_out, notconnected_6_out[5]);
  not not_12 (not_12_out, notconnected_6_out[4]);
  and and_124 (and_124_out, notconnected_4_out, notconnected_6_out[4]);
  not not_13 (not_13_out, notconnected_6_out[3]);
  and and_125 (and_125_out, notconnected_4_out, notconnected_6_out[3]);
  not not_14 (not_14_out, notconnected_6_out[2]);
  and and_126 (and_126_out, notconnected_4_out, notconnected_6_out[2]);
  not not_15 (not_15_out, notconnected_6_out[1]);
  and and_127 (and_127_out, notconnected_4_out, notconnected_6_out[1]);
  not not_16 (not_16_out, notconnected_6_out[0]);
  and and_128 (and_128_out, notconnected_4_out, notconnected_6_out[0]);
  and and_129 (and_129_out, not_17_out, dipswitch_4_out);
  not not_17 (not_17_out, dipswitch_5_out);
  and and_130 (and_130_out, dipswitch_4_out, dipswitch_5_out);
  and and_131 (and_131_out, not_9_out, notconnected_4_out);
  and and_132 (and_132_out, not_10_out, notconnected_4_out);
  and and_133 (and_133_out, not_11_out, notconnected_4_out);
  and and_134 (and_134_out, not_12_out, notconnected_4_out);
  and and_135 (and_135_out, not_13_out, notconnected_4_out);
  and and_136 (and_136_out, not_14_out, notconnected_4_out);
  and and_137 (and_137_out, not_15_out, notconnected_4_out);
  and and_138 (and_138_out, not_16_out, notconnected_4_out);
  nor nor_9 (nor_9_out, and_131_out, nor_10_out);
  nor nor_10 (nor_10_out, nor_9_out, and_121_out);
  nor nor_11 (nor_11_out, and_132_out, nor_12_out);
  nor nor_12 (nor_12_out, nor_11_out, and_122_out);
  nor nor_13 (nor_13_out, and_133_out, nor_14_out);
  nor nor_14 (nor_14_out, nor_13_out, and_123_out);
  nor nor_15 (nor_15_out, and_134_out, nor_16_out);
  nor nor_16 (nor_16_out, nor_15_out, and_124_out);
  nor nor_17 (nor_17_out, and_135_out, nor_18_out);
  nor nor_18 (nor_18_out, nor_17_out, and_125_out);
  nor nor_19 (nor_19_out, and_136_out, nor_20_out);
  nor nor_20 (nor_20_out, nor_19_out, and_126_out);
  nor nor_21 (nor_21_out, and_137_out, nor_22_out);
  nor nor_22 (nor_22_out, nor_21_out, and_127_out);
  nor nor_23 (nor_23_out, and_138_out, nor_24_out);
  nor nor_24 (nor_24_out, nor_23_out, and_128_out);
  nand nand_73 (nand_73_out, nand_58_out, nand_74_out);
  nand nand_74 (nand_74_out, nand_73_out, nand_59_out);
  and and_139 (and_139_out, nand_73_out, notconnected_3_out);
  nand nand_75 (nand_75_out, nand_62_out, nand_76_out);
  nand nand_76 (nand_76_out, nand_75_out, nand_63_out);
  and and_140 (and_140_out, nand_75_out, notconnected_3_out);
  nand nand_77 (nand_77_out, nand_66_out, nand_78_out);
  nand nand_78 (nand_78_out, nand_77_out, nand_67_out);
  and and_141 (and_141_out, nand_77_out, notconnected_3_out);
  nand nand_79 (nand_79_out, nand_70_out, nand_80_out);
  nand nand_80 (nand_80_out, nand_79_out, nand_71_out);
  and and_142 (and_142_out, nand_79_out, notconnected_3_out);
  and and_143 (and_143_out, notconnected_7_out[7], notconnected_8_out[7]);
  xor xor_41 (xor_41_out, notconnected_8_out[7], notconnected_7_out[7]);
  and and_144 (and_144_out, notconnected_7_out[6], notconnected_8_out[6]);
  xor xor_42 (xor_42_out, notconnected_8_out[6], notconnected_7_out[6]);
  and and_145 (and_145_out, notconnected_7_out[5], notconnected_8_out[5]);
  xor xor_43 (xor_43_out, notconnected_8_out[5], notconnected_7_out[5]);
  and and_146 (and_146_out, notconnected_7_out[4], notconnected_8_out[4]);
  xor xor_44 (xor_44_out, notconnected_8_out[4], notconnected_7_out[4]);
  and and_147 (and_147_out, notconnected_7_out[3], notconnected_8_out[3]);
  xor xor_45 (xor_45_out, notconnected_8_out[3], notconnected_7_out[3]);
  and and_148 (and_148_out, notconnected_7_out[2], notconnected_8_out[2]);
  xor xor_46 (xor_46_out, notconnected_8_out[2], notconnected_7_out[2]);
  and and_149 (and_149_out, notconnected_7_out[1], notconnected_8_out[1]);
  xor xor_47 (xor_47_out, notconnected_8_out[1], notconnected_7_out[1]);
  and and_150 (and_150_out, notconnected_7_out[0], notconnected_8_out[0]);
  xor xor_48 (xor_48_out, notconnected_8_out[0], notconnected_7_out[0]);
  nor nor_25 (nor_25_out, and_129_out, nor_26_out);
  nor nor_26 (nor_26_out, nor_25_out, and_130_out);
  or or_66 (or_66_out, and_143_out, and_151_out);
  and and_151 (and_151_out, xor_41_out, or_67_out);
  xor xor_49 (xor_49_out, xor_41_out, or_67_out);
  or or_67 (or_67_out, and_144_out, and_152_out);
  and and_152 (and_152_out, xor_42_out, or_68_out);
  xor xor_50 (xor_50_out, xor_42_out, or_68_out);
  or or_68 (or_68_out, and_145_out, and_153_out);
  and and_153 (and_153_out, xor_43_out, or_69_out);
  xor xor_51 (xor_51_out, xor_43_out, or_69_out);
  or or_69 (or_69_out, and_146_out, and_154_out);
  and and_154 (and_154_out, xor_44_out, or_70_out);
  xor xor_52 (xor_52_out, xor_44_out, or_70_out);
  or or_70 (or_70_out, and_147_out, and_163_out);
  or or_71 (or_71_out, and_148_out, and_164_out);
  or or_72 (or_72_out, and_149_out, and_165_out);
  or or_73 (or_73_out, and_150_out, and_166_out);
  // NotConnected on notconnected_9_out
  Reset reset_1 ();  // open: out
  Reset reset_2 ();  // open: out
  and and_155 (and_155_out, nor_9_out, notconnected_5_out);
  Reset reset_3 ();  // open: out
  and and_156 (and_156_out, nor_11_out, notconnected_5_out);
  Reset reset_4 ();  // open: out
  and and_157 (and_157_out, nor_13_out, notconnected_5_out);
  Reset reset_5 ();  // open: out
  and and_158 (and_158_out, nor_15_out, notconnected_5_out);
  Reset reset_6 ();  // open: out
  and and_159 (and_159_out, nor_17_out, notconnected_5_out);
  Reset reset_7 ();  // open: out
  and and_160 (and_160_out, nor_19_out, notconnected_5_out);
  Reset reset_8 ();  // open: out
  and and_161 (and_161_out, nor_21_out, notconnected_5_out);
  Reset reset_9 ();  // open: out
  and and_162 (and_162_out, nor_23_out, notconnected_5_out);
  and and_163 (and_163_out, xor_45_out, or_71_out);
  xor xor_53 (xor_53_out, xor_45_out, or_71_out);
  and and_164 (and_164_out, xor_46_out, or_72_out);
  xor xor_54 (xor_54_out, xor_46_out, or_72_out);
  and and_165 (and_165_out, xor_47_out, or_73_out);
  xor xor_55 (xor_55_out, xor_47_out, or_73_out);
  and and_166 (and_166_out, xor_48_out, notconnected_9_out);
  xor xor_56 (xor_56_out, xor_48_out, notconnected_9_out);
  and and_167 (and_167_out, nor_25_out, dipswitch_3_out);
  nand nand_81 (nand_81_out, nand_84_out, nand_82_out);
  nand nand_82 (nand_82_out, nand_81_out, notconnected_2_out);
  nand nand_83 (nand_83_out, nand_82_out, notconnected_2_out, nand_84_out);
  nand nand_84 (nand_84_out, nand_83_out, notconnected_1_out[7]);
  nand nand_85 (nand_85_out, nand_88_out, nand_86_out);
  nand nand_86 (nand_86_out, nand_85_out, notconnected_2_out);
  nand nand_87 (nand_87_out, nand_86_out, notconnected_2_out, nand_88_out);
  nand nand_88 (nand_88_out, nand_87_out, notconnected_1_out[5]);
  nand nand_89 (nand_89_out, nand_92_out, nand_90_out);
  nand nand_90 (nand_90_out, nand_89_out, notconnected_2_out);
  nand nand_91 (nand_91_out, nand_90_out, notconnected_2_out, nand_92_out);
  nand nand_92 (nand_92_out, nand_91_out, notconnected_1_out[3]);
  nand nand_93 (nand_93_out, nand_96_out, nand_94_out);
  nand nand_94 (nand_94_out, nand_93_out, notconnected_2_out);
  nand nand_95 (nand_95_out, nand_94_out, notconnected_2_out, nand_96_out);
  nand nand_96 (nand_96_out, nand_95_out, notconnected_1_out[1]);
  nand nand_97 (nand_97_out, nand_82_out, nand_98_out);
  nand nand_98 (nand_98_out, nand_97_out, nand_83_out);
  and and_168 (and_168_out, nand_97_out, notconnected_3_out);
  nand nand_99 (nand_99_out, nand_86_out, nand_100_out);
  nand nand_100 (nand_100_out, nand_99_out, nand_87_out);
  and and_169 (and_169_out, nand_99_out, notconnected_3_out);
  nand nand_101 (nand_101_out, nand_90_out, nand_102_out);
  nand nand_102 (nand_102_out, nand_101_out, nand_91_out);
  and and_170 (and_170_out, nand_101_out, notconnected_3_out);
  nand nand_103 (nand_103_out, nand_94_out, nand_104_out);
  nand nand_104 (nand_104_out, nand_103_out, nand_95_out);
  and and_171 (and_171_out, nand_103_out, notconnected_3_out);
  // NotConnected on notconnected_10_out
  // NotConnected on notconnected_11_out
  // NotConnected on notconnected_12_out
  // NotConnected on notconnected_13_out
  and and_172 (and_172_out, notconnected_11_out[0], notconnected_11_out[0]);
  or or_74 (or_74_out, notconnected_12_out[0], notconnected_12_out[0]);
  xor xor_57 (xor_57_out, notconnected_13_out[0], notconnected_13_out[0]);
  and and_173 (and_173_out, notconnected_11_out[1], notconnected_11_out[1]);
  or or_75 (or_75_out, notconnected_12_out[1], notconnected_12_out[1]);
  xor xor_58 (xor_58_out, notconnected_13_out[1], notconnected_13_out[1]);
  not not_18 (not_18_out, notconnected_14_out);
  // NotConnected on notconnected_14_out
  and and_174 (and_174_out, notconnected_11_out[2], notconnected_11_out[2]);
  and and_175 (and_175_out, notconnected_11_out[3], notconnected_11_out[3]);
  or or_76 (or_76_out, notconnected_12_out[2], notconnected_12_out[2]);
  or or_77 (or_77_out, notconnected_12_out[3], notconnected_12_out[3]);
  xor xor_59 (xor_59_out, notconnected_13_out[2], notconnected_13_out[2]);
  xor xor_60 (xor_60_out, notconnected_13_out[3], notconnected_13_out[3]);
  // And and_176 has open pins: In_1=and_177_out, In_2=notconnected_10_out[7], out=open
  xor xor_61 (xor_61_out, notconnected_10_out[7], and_177_out);
  and and_177 (and_177_out, and_178_out, notconnected_10_out[6]);
  xor xor_62 (xor_62_out, notconnected_10_out[6], and_178_out);
  and and_178 (and_178_out, and_179_out, notconnected_10_out[5]);
  xor xor_63 (xor_63_out, notconnected_10_out[5], and_179_out);
  and and_179 (and_179_out, and_180_out, notconnected_10_out[4]);
  xor xor_64 (xor_64_out, notconnected_10_out[4], and_180_out);
  and and_180 (and_180_out, and_181_out, notconnected_10_out[3]);
  xor xor_65 (xor_65_out, notconnected_10_out[3], and_181_out);
  and and_181 (and_181_out, and_182_out, notconnected_10_out[2]);
  xor xor_66 (xor_66_out, notconnected_10_out[2], and_182_out);
  and and_182 (and_182_out, and_183_out, notconnected_10_out[1]);
  xor xor_67 (xor_67_out, notconnected_10_out[1], and_183_out);
  and and_183 (and_183_out, not_18_out, notconnected_10_out[0]);
  xor xor_68 (xor_68_out, notconnected_10_out[0], not_18_out);
  and and_184 (and_184_out, notconnected_11_out[4], notconnected_11_out[4]);
  or or_78 (or_78_out, notconnected_12_out[4], notconnected_12_out[4]);
  xor xor_69 (xor_69_out, notconnected_13_out[4], notconnected_13_out[4]);
  and and_185 (and_185_out, notconnected_11_out[5], notconnected_11_out[5]);
  or or_79 (or_79_out, notconnected_12_out[5], notconnected_12_out[5]);
  xor xor_70 (xor_70_out, notconnected_13_out[5], notconnected_13_out[5]);
  and and_186 (and_186_out, notconnected_11_out[6], notconnected_11_out[6]);
  and and_187 (and_187_out, notconnected_11_out[7], notconnected_11_out[7]);
  or or_80 (or_80_out, notconnected_12_out[6], notconnected_12_out[6]);
  or or_81 (or_81_out, notconnected_12_out[7], notconnected_12_out[7]);
  xor xor_71 (xor_71_out, notconnected_13_out[6], notconnected_13_out[6]);
  xor xor_72 (xor_72_out, notconnected_13_out[7], notconnected_13_out[7]);
  // NotConnected on notconnected_15_out
  // NotConnected on notconnected_16_out
  // NotConnected on notconnected_17_out
  // NotConnected on notconnected_18_out
  // NotConnected on notconnected_19_out
  // NotConnected on notconnected_20_out
  and and_188 (and_188_out, notconnected_21_out, notconnected_15_out[0]);
  nand nand_105 (nand_105_out, notconnected_16_out[0], notconnected_16_out[0]);
  nor nor_27 (nor_27_out, notconnected_17_out[0], notconnected_17_out[0]);
  not not_19 (not_19_out, notconnected_20_out);
  and and_189 (and_189_out, notconnected_21_out, notconnected_15_out[1]);
  and and_190 (and_190_out, notconnected_21_out, notconnected_15_out[2]);
  nand nand_106 (nand_106_out, notconnected_16_out[1], notconnected_16_out[1]);
  nand nand_107 (nand_107_out, notconnected_16_out[2], notconnected_16_out[2]);
  nor nor_28 (nor_28_out, notconnected_17_out[1], notconnected_17_out[1]);
  nor nor_29 (nor_29_out, notconnected_17_out[2], notconnected_17_out[2]);
  not not_20 (not_20_out, notconnected_19_out);
  not not_21 (not_21_out, notconnected_18_out);
  not not_22 (not_22_out, notconnected_20_out);
  not not_23 (not_23_out, notconnected_19_out);
  not not_24 (not_24_out, notconnected_18_out);
  not not_25 (not_25_out, not_19_out);
  // NotConnected on notconnected_21_out
  and and_191 (and_191_out, notconnected_21_out, notconnected_15_out[3]);
  nand nand_108 (nand_108_out, notconnected_16_out[3], notconnected_16_out[3]);
  nor nor_30 (nor_30_out, notconnected_17_out[3], notconnected_17_out[3]);
  and and_192 (and_192_out, not_21_out, not_20_out);
  and and_193 (and_193_out, notconnected_18_out, not_20_out);
  and and_194 (and_194_out, not_21_out, notconnected_19_out);
  and and_195 (and_195_out, notconnected_19_out, notconnected_18_out);
  and and_196 (and_196_out, not_24_out, not_23_out);
  and and_197 (and_197_out, notconnected_18_out, not_23_out);
  and and_198 (and_198_out, not_24_out, notconnected_19_out);
  and and_199 (and_199_out, notconnected_19_out, notconnected_18_out);
  and and_200 (and_200_out, notconnected_21_out, notconnected_15_out[4]);
  nand nand_109 (nand_109_out, notconnected_16_out[4], notconnected_16_out[4]);
  nor nor_31 (nor_31_out, notconnected_17_out[4], notconnected_17_out[4]);
  and and_201 (and_201_out, and_192_out, not_22_out);
  and and_202 (and_202_out, and_193_out, not_22_out);
  and and_203 (and_203_out, and_194_out, not_22_out);
  and and_204 (and_204_out, and_195_out, not_22_out);
  and and_205 (and_205_out, and_196_out, not_25_out);
  and and_206 (and_206_out, and_197_out, not_25_out);
  and and_207 (and_207_out, and_198_out, not_25_out);
  and and_208 (and_208_out, and_199_out, not_25_out);
  and and_209 (and_209_out, notconnected_21_out, notconnected_15_out[5]);
  and and_210 (and_210_out, notconnected_21_out, notconnected_15_out[6]);
  nand nand_110 (nand_110_out, notconnected_16_out[5], notconnected_16_out[5]);
  nand nand_111 (nand_111_out, notconnected_16_out[6], notconnected_16_out[6]);
  nor nor_32 (nor_32_out, notconnected_17_out[5], notconnected_17_out[5]);
  nor nor_33 (nor_33_out, notconnected_17_out[6], notconnected_17_out[6]);
  and and_211 (and_211_out, notconnected_21_out, notconnected_15_out[7]);
  nand nand_112 (nand_112_out, notconnected_16_out[7], notconnected_16_out[7]);
  nor nor_34 (nor_34_out, notconnected_17_out[7], notconnected_17_out[7]);
  // Pins of 1 and 8 bits meet at notconnected_1_out

  // Notes on the sheet:
  //   Overwrite Value
  //   Overwrite
  //   COUNTER
  //   B
  //   Select
  //   MUX
  //   A
  //   INCRMNT
  //   SWITCH
  //   OR
  //   Edge Flop
  //   D
  //   Clk
  //   Load
  //   Latch
  //   Always
  //   Loaded
  //   ALU
  //   ADDER
  //   AND
  //   NAND
  //   NOR
  //   XOR
  //   .
  //   3x8 Demux
  //   A1
  //   A2
  //   A3
  //   2x4 Demux
  //   A_0
  //   A_1
  //   Disable
  //   COMPONENTS
  //   Register - outdated
  //   Save
  //   Save Value
  //   Edge Register
  //   1 Bit mem
  //   SaveVal
  //   Reset
  //   Write
  //   Always OUT
  //   OUT
  //   Always On Out
  //   Out
endmodule

/* Test case:
D C L ALWAYS LOADED
# 1. Randomized Startup: Register state is unknown (X). LOADED is 0 because L=0.
0x00 0 0 X 0x00

# 2. Load 0xAA: ALWAYS updates to 0xAA. LOADED shows it because L=1.
0xAA C 1 0xAA 0xAA

# 3. Transparent Check: ALWAYS stays 0xAA. LOADED drops to 0x00 because L=0.
0x55 0 0 0xAA 0x00
0x21 C 0 0x21 0x00

# 5. Load 0x00: Register becomes 0. Both pins show 0.
0x00 C 1 0x00 0x00

# 6. Edge-Triggering: Data 0xEE only moves to ALWAYS on the rising edge.
0xEE 0 1 0x00 0x00  # L=1, but no clock yet; LOADED is 0 because reg is 0
0xEE 1 1 0xEE 0xEE  # Clock goes high; Reg becomes 0xEE. LOADED now shows it.
0xDD 0 1 0xEE 0xEE  # Clock falls; Reg stays 0xEE.

# 7. High-Clock Stability Test
0xAA 0 1 0xEE 0xEE  # Prepare data 0xAA, but clock is 0. ALWAYS stays 0xEE.
0xAA 1 1 0xAA 0xAA  # Clock goes High. Register captures 0xAA.
0xFF 1 1 0xAA 0xAA  # DATA CHANGES TO 0xFF WHILE CLOCK IS STILL HIGH.
                    # ALWAYS MUST STAY 0xAA. If it changes to 0xFF, it's a latch!
*/

/* Test case:
C_2 C_1 C_0 A_0 B_0 O_0
0 0 1 9 6 15 #addition and subtraction
0 1 0 9 6 3
0 0 1 6 7 13
0 1 0 111 67 44
0 0 1 32 59 91
0 1 1 51 60 48  #and
0 1 1 3 2 2
0 1 1 5 3 1
0 1 1 12 25 8
0 1 1 4 8 0
1 0 1 5 3 7 #or
1 0 1 2 8 10
1 0 1 12 25 29
1 0 1 0 7 7
1 0 0 1 1 254 #nand
1 0 0 2 4 255
1 0 0 15 3 252
1 1 0 1 0 254 #nor
1 1 0 3 5 248
1 1 0 128 64 63
1 1 1 5 3 6 #xor
1 1 1 10 10 0
1 1 1 85 170 255
1 1 1 14 1 15
*/
